// Logisim project GPR.circ as structural Verilog: 2 circuits, main circuit GPR_16x32bit
module GPR_16x32bit (
  input  clk,
  input  [31:0] wdata,
  input  [3:0] waddr,
  input  wenable,
  input  [3:0] raddr1,
  input  [3:0] raddr2,
  input  reset,
  input  reset_r0,
  output [31:0] rdata1,
  output [31:0] rdata2
);

  wire decoder_1_out0, decoder_1_out1, decoder_1_out2, decoder_1_out3, decoder_1_out4, decoder_1_out5,
       decoder_1_out6, decoder_1_out7, decoder_1_out8, decoder_1_out9, decoder_1_out10, decoder_1_out11,
       decoder_1_out12, decoder_1_out13, decoder_1_out14, decoder_1_out15, or_1_out;
  wire [31:0] register_1_q, register_2_q, register_3_q, register_4_q, register_5_q, register_6_q,
       register_7_q, register_8_q, register_9_q, register_10_q, register_11_q, register_12_q, register_13_q,
       register_14_q, register_15_q, register_16_q;

  Decoder #(.select(4)) decoder_1 (
    .out0(decoder_1_out0), .out1(decoder_1_out1), .out2(decoder_1_out2), .out3(decoder_1_out3),
    .out4(decoder_1_out4), .out5(decoder_1_out5), .out6(decoder_1_out6), .out7(decoder_1_out7),
    .out8(decoder_1_out8), .out9(decoder_1_out9), .out10(decoder_1_out10), .out11(decoder_1_out11),
    .out12(decoder_1_out12), .out13(decoder_1_out13), .out14(decoder_1_out14), .out15(decoder_1_out15),
    .sel(waddr), .en(wenable));
  Register #(.width(32)) register_1 (.D(wdata), .en(decoder_1_out0), .clk(clk), .Q(register_1_q), .clr(or_1_out));
  Register #(.width(32)) register_2 (.D(wdata), .en(decoder_1_out8), .clk(clk), .Q(register_2_q), .clr(reset));
  Register #(.width(32)) register_3 (.D(wdata), .en(decoder_1_out1), .clk(clk), .Q(register_3_q), .clr(reset));
  or or_1 (or_1_out, reset_r0, reset);
  Register #(.width(32)) register_4 (.D(wdata), .en(decoder_1_out9), .clk(clk), .Q(register_4_q), .clr(reset));
  Register #(.width(32)) register_5 (.D(wdata), .en(decoder_1_out2), .clk(clk), .Q(register_5_q), .clr(reset));
  Register #(.width(32)) register_6 (.D(wdata), .en(decoder_1_out10), .clk(clk), .Q(register_6_q), .clr(reset));
  Register #(.width(32)) register_7 (.D(wdata), .en(decoder_1_out3), .clk(clk), .Q(register_7_q), .clr(reset));
  Register #(.width(32)) register_8 (.D(wdata), .en(decoder_1_out11), .clk(clk), .Q(register_8_q), .clr(reset));
  Register #(.width(32)) register_9 (.D(wdata), .en(decoder_1_out4), .clk(clk), .Q(register_9_q), .clr(reset));
  Register #(.width(32)) register_10 (.D(wdata), .en(decoder_1_out12), .clk(clk), .Q(register_10_q), .clr(reset));
  Register #(.width(32)) register_11 (.D(wdata), .en(decoder_1_out5), .clk(clk), .Q(register_11_q), .clr(reset));
  Register #(.width(32)) register_12 (.D(wdata), .en(decoder_1_out13), .clk(clk), .Q(register_12_q), .clr(reset));
  Register #(.width(32)) register_13 (.D(wdata), .en(decoder_1_out6), .clk(clk), .Q(register_13_q), .clr(reset));
  Register #(.width(32)) register_14 (.D(wdata), .en(decoder_1_out14), .clk(clk), .Q(register_14_q), .clr(reset));
  Register #(.width(32)) register_15 (.D(wdata), .en(decoder_1_out7), .clk(clk), .Q(register_15_q), .clr(reset));
  Register #(.width(32)) register_16 (.D(wdata), .en(decoder_1_out15), .clk(clk), .Q(register_16_q), .clr(reset));
  Multiplexer #(.select(4), .width(32)) multiplexer_1 (
    .in0(register_1_q), .in1(register_3_q), .in2(register_5_q), .in3(register_7_q), .in4(register_9_q),
    .in5(register_11_q), .in6(register_13_q), .in7(register_15_q), .in8(register_2_q), .in9(register_4_q),
    .in10(register_6_q), .in11(register_8_q), .in12(register_10_q), .in13(register_12_q),
    .in14(register_14_q), .in15(register_16_q), .out(rdata1), .sel(raddr1));
  Multiplexer #(.select(4), .width(32)) multiplexer_2 (
    .in0(register_1_q), .in1(register_3_q), .in2(register_5_q), .in3(register_7_q), .in4(register_9_q),
    .in5(register_11_q), .in6(register_13_q), .in7(register_15_q), .in8(register_2_q), .in9(register_4_q),
    .in10(register_6_q), .in11(register_8_q), .in12(register_10_q), .in13(register_12_q),
    .in14(register_14_q), .in15(register_16_q), .out(rdata2), .sel(raddr2));
endmodule

module GPR_32x32bit (
  input  clk,
  input  [31:0] wdata,
  input  [4:0] waddr,
  input  wenable,
  input  reset,
  input  [4:0] raddr1,
  input  [4:0] raddr2,
  output [31:0] rdata1,
  output [31:0] rdata2
);

  wire and_1_out, and_2_out, not_1_out;
  wire [31:0] GPR_0_rdata1, GPR_0_rdata2, GPR_1_rdata1, GPR_1_rdata2;

  not not_1 (not_1_out, waddr[4]);
  and and_1 (and_1_out, not_1_out, wenable);
  and and_2 (and_2_out, waddr[4], wenable);
  GPR_16x32bit GPR_0 (
    .clk(clk), .wdata(wdata), .waddr(waddr[3:0]), .wenable(and_1_out), .raddr1(raddr1[3:0]),
    .raddr2(raddr2[3:0]), .reset(reset), .reset_r0(1'b1), .rdata1(GPR_0_rdata1), .rdata2(GPR_0_rdata2));
  GPR_16x32bit GPR_1 (
    .clk(clk), .wdata(wdata), .waddr(waddr[3:0]), .wenable(and_2_out), .raddr1(raddr1[3:0]),
    .raddr2(raddr2[3:0]), .reset(reset), .reset_r0(1'b0), .rdata1(GPR_1_rdata1), .rdata2(GPR_1_rdata2));
  Multiplexer #(.width(32)) multiplexer_1 (.in0(GPR_0_rdata1), .in1(GPR_1_rdata1), .out(rdata1), .sel(raddr1[4]));
  Multiplexer #(.width(32)) multiplexer_2 (.in0(GPR_0_rdata2), .in1(GPR_1_rdata2), .out(rdata2), .sel(raddr2[4]));
endmodule
