// Logisim project minirv.circ as structural Verilog: 18 circuits, main circuit minirv
module minirv (
  input  reset
);

  wire clock_1_out, jump_enable, mem_byte_access, mem_renable, mem_wenable, wenable;
  wire [4:0] raddr1, raddr2, waddr;
  wire [31:0] instruction, jump_addr, mem_addr, mem_wdata, memory_1_mem_rdata, next_addr, rdata1, rdata2,
       wdata;

  Clock clock_1 (.out(clock_1_out));
  cycle_counter cycle_counter_1 (.clk(clock_1_out), .reset(reset));
  fetcher fetcher_1 (
    .jump_addr(jump_addr), .jump_enable(jump_enable), .clk(clock_1_out), .reset(reset),
    .next_addr(next_addr), .instruction(instruction));
  GPR_32x32bit gpr_32x32bit_1 (
    .clk(clock_1_out), .wdata(wdata), .waddr(waddr), .wenable(wenable), .reset(reset), .raddr1(raddr1),
    .raddr2(raddr2), .rdata1(rdata1), .rdata2(rdata2));
  memory memory_1 (
    .mem_wenable(mem_wenable), .mem_byte_access(mem_byte_access), .mem_wdata(mem_wdata), .mem_addr(mem_addr),
    .clk(clock_1_out), .reset(reset), .mem_rdata(memory_1_mem_rdata));
  executor executor_1 (
    .instruction(instruction), .rdata1(rdata1), .rdata2(rdata2), .next_addr(next_addr),
    .mem_rdata(memory_1_mem_rdata), .raddr1(raddr1), .raddr2(raddr2), .waddr(waddr), .wenable(wenable),
    .wdata(wdata), .jump_addr(jump_addr), .jump_enable(jump_enable), .mem_addr(mem_addr),
    .mem_wenable(mem_wenable), .mem_renable(mem_renable), .mem_byte_access(mem_byte_access),
    .mem_wdata(mem_wdata));
endmodule

module i_decoder (
  input  [31:0] instruction,
  output [6:0] opcode,
  output [4:0] rd,
  output [2:0] funct3,
  output [4:0] rs1,
  output [11:0] imm
);


  assign funct3 = instruction[14:12];
  assign imm = instruction[31:20];
  assign opcode = instruction[6:0];
  assign rd = instruction[11:7];
  assign rs1 = instruction[19:15];
endmodule

module instruction_identifier (
  input  [31:0] instruction,
  output is_addi,
  output is_jalr,
  output is_add,
  output is_lui,
  output is_lw,
  output is_sw,
  output is_lbu,
  output is_sb
);

  wire comparator_1_eq, comparator_2_eq, comparator_3_eq, comparator_4_eq, comparator_5_eq, comparator_6_eq,
       comparator_7_eq, comparator_8_eq, comparator_9_eq, comparator_10_eq, comparator_11_eq,
       comparator_12_eq, comparator_14_eq, comparator_15_eq;
  wire [2:0] i_decoder_1_funct3, i_decoder_2_funct3, i_decoder_3_funct3, r_decoder_1_funct3,
       s_decoder_1_funct3, s_decoder_2_funct3;
  wire [6:0] i_decoder_1_opcode, i_decoder_2_opcode, i_decoder_3_opcode, r_decoder_1_opcode,
       s_decoder_1_opcode, s_decoder_2_opcode, u_decoder_1_opcode;

  i_decoder i_decoder_1 (
    .instruction(instruction), .opcode(i_decoder_1_opcode), .funct3(i_decoder_1_funct3));  // open: rd, rs1, imm
  r_decoder r_decoder_1 (
    .instruction(instruction), .opcode(r_decoder_1_opcode), .funct3(r_decoder_1_funct3));  // open: rd, rs1, rs2, funct7
  u_decoder u_decoder_1 (.instruction(instruction), .opcode(u_decoder_1_opcode));  // open: rd, imm
  i_decoder i_decoder_2 (
    .instruction(instruction), .opcode(i_decoder_2_opcode), .funct3(i_decoder_2_funct3));  // open: rd, rs1, imm
  s_decoder s_decoder_1 (
    .instruction(instruction), .opcode(s_decoder_1_opcode), .funct3(s_decoder_1_funct3));  // open: rs1, rs2, imm
  i_decoder i_decoder_3 (
    .instruction(instruction), .opcode(i_decoder_3_opcode), .funct3(i_decoder_3_funct3));  // open: rd, rs1, imm
  s_decoder s_decoder_2 (
    .instruction(instruction), .opcode(s_decoder_2_opcode), .funct3(s_decoder_2_funct3));  // open: rs1, rs2, imm
  Comparator #(.mode("unsigned"), .width(7)) comparator_1 (
    .a(7'b0100011), .b(s_decoder_1_opcode), .eq(comparator_1_eq));  // open: gt, lt
  Comparator #(.mode("unsigned"), .width(3)) comparator_2 (
    .a(s_decoder_1_funct3), .b(3'b010), .eq(comparator_2_eq));  // open: gt, lt
  Comparator #(.mode("unsigned"), .width(7)) comparator_3 (
    .a(7'b0000011), .b(i_decoder_3_opcode), .eq(comparator_3_eq));  // open: gt, lt
  Comparator #(.mode("unsigned"), .width(3)) comparator_4 (
    .a(i_decoder_3_funct3), .b(3'b100), .eq(comparator_4_eq));  // open: gt, lt
  Comparator #(.mode("unsigned"), .width(7)) comparator_5 (
    .a(7'b0100011), .b(s_decoder_2_opcode), .eq(comparator_5_eq));  // open: gt, lt
  Comparator #(.mode("unsigned"), .width(3)) comparator_6 (
    .a(s_decoder_2_funct3), .b(3'b000), .eq(comparator_6_eq));  // open: gt, lt
  Comparator #(.mode("unsigned"), .width(3)) comparator_7 (
    .a(3'b000), .b(i_decoder_1_funct3), .eq(comparator_7_eq));  // open: gt, lt
  Comparator #(.mode("unsigned"), .width(7)) comparator_8 (
    .a(7'b0010011), .b(i_decoder_1_opcode), .eq(comparator_8_eq));  // open: gt, lt
  Comparator #(.mode("unsigned"), .width(3)) comparator_9 (
    .a(3'b000), .b(i_decoder_1_funct3), .eq(comparator_9_eq));  // open: gt, lt
  Comparator #(.mode("unsigned"), .width(7)) comparator_10 (
    .a(7'b1100111), .b(i_decoder_1_opcode), .eq(comparator_10_eq));  // open: gt, lt
  Comparator #(.mode("unsigned"), .width(7)) comparator_11 (
    .a(7'b0110011), .b(r_decoder_1_opcode), .eq(comparator_11_eq));  // open: gt, lt
  Comparator #(.mode("unsigned"), .width(3)) comparator_12 (
    .a(3'b000), .b(r_decoder_1_funct3), .eq(comparator_12_eq));  // open: gt, lt
  Comparator #(.mode("unsigned"), .width(7)) comparator_13 (
    .a(7'b0110111), .b(u_decoder_1_opcode), .eq(is_lui));  // open: gt, lt
  Comparator #(.mode("unsigned"), .width(7)) comparator_14 (
    .a(7'b0000011), .b(i_decoder_2_opcode), .eq(comparator_14_eq));  // open: gt, lt
  Comparator #(.mode("unsigned"), .width(3)) comparator_15 (
    .a(3'b010), .b(i_decoder_2_funct3), .eq(comparator_15_eq));  // open: gt, lt
  and and_1 (is_add, comparator_11_eq, comparator_12_eq);
  and and_2 (is_lw, comparator_14_eq, comparator_15_eq);
  and and_3 (is_sw, comparator_1_eq, comparator_2_eq);
  and and_4 (is_lbu, comparator_3_eq, comparator_4_eq);
  and and_5 (is_sb, comparator_5_eq, comparator_6_eq);
  and and_6 (is_addi, comparator_7_eq, comparator_8_eq);
  and and_7 (is_jalr, comparator_9_eq, comparator_10_eq);
endmodule

module fetcher (
  input  [31:0] jump_addr,
  input  jump_enable,
  input  clk,
  input  reset,
  output [31:0] next_addr,
  output [31:0] instruction
);

  wire [23:0] PC_q_2;
  wire [31:0] multiplexer_1_out, PC_q;

  Multiplexer #(.width(32)) multiplexer_1 (
    .in0(next_addr), .in1(jump_addr), .out(multiplexer_1_out), .sel(jump_enable));
  ROM #(.addrWidth(24), .dataWidth(32)) rom_1 (.addr(PC_q_2), .data(instruction));
  Register #(.width(32)) PC (
    .D(multiplexer_1_out), .en(1'b1), .clk(clk), .Q({PC_q[31:26], PC_q_2, PC_q[1:0]}), .clr(reset));
  Adder #(.width(32)) adder_1 (.a(32'h4), .b({PC_q[31:26], PC_q_2, PC_q[1:0]}), .out(next_addr));  // open: cin, cout

  // Notes on the sheet:
  //   contents of rom_1 (hex, n*v repeats v):
  //   413 51137 10113 22c00093 80e7 fea12823 fe812e23 40800413 ff014183 3401b3 1c183 ff114203 440233 24203
  //   4181b3 ff214203 440233 24203 4181b3 ff314203 440233 24203 4181b3 40000213 320233 24203 ffc12403
  //   420233 420233 410233 9400193 fe312823 9000193 fe312623 fec22203 20067 8067 ff410113 100513 112423
  //   22400093 80e7 ff010113 112623 12023 100793 6500693 12703 f70733 e12023 178793 fef12823 fed12623
  //   fe812e23 fe912c23 30000413 ff014183 340233 100193 320023 fec14183 3401b3 18023 24183 ff114483 940233
  //   100493 920023 fed14483 9404b3 48023 24483 9181b3 ff214483 940233 100493 920023 fee14483 9404b3 48023
  //   24483 9181b3 ff314483 940233 100493 920023 fef14483 9404b3 48023 24483 9181b3 40000213 320233 24203
  //   ff812483 ffc12403 420233 420233 410233 1a400193 fe312823 bc00193 fe312623 fec22203 20067 12503
  //   fffff7b7 c4678793 f50533 fea12823 fe812e23 40800413 ff014183 3401b3 1c183 ff114203 440233 24203
  //   4181b3 ff214203 440233 24203 4181b3 ff314203 440233 24203 4181b3 40000213 320233 24503 ffc12403
  //   1400093 80e7 c12083 513 1010113 8067 22400213 20067 ff410113 48537 60050513 112423 a800093 80e7
  //   22400093 80e7 109*0 1 0 1010100 63*1010101 100 1000101 1010100 1000000 1010100 121*0 64*1000100
  //   64*2020000 64*3020100 0 4040404 0 4040404 0 4040404 0 4040404 0 4040404 0 4040404 0 4040404 0
  //   4040404 0 4040404 0 4040404 0 4040404 0 4040404 0 4040404 0 4040404 0 4040404 0 4040404 0 4040404 0
  //   4040404 0 4040404 0 4040404 0 4040404 0 4040404 0 4040404 0 4040404 0 4040404 0 4040404 0 4040404 0
  //   4040404 0 4040404 0 4040404 0 4040404 0 4040404 1000100 5040504 1000100 5040504 1000100 5040504
  //   1000100 5040504 1000100 5040504 1000100 5040504 1000100 5040504 1000100 5040504 1000100 5040504
  //   1000100 5040504 1000100 5040504 1000100 5040504 1000100 5040504 1000100 5040504 1000100 5040504
  //   1000100 5040504 1000100 5040504 1000100 5040504 1000100 5040504 1000100 5040504 1000100 5040504
  //   1000100 5040504 1000100 5040504 1000100 5040504 1000100 5040504 1000100 5040504 1000100 5040504
  //   1000100 5040504 1000100 5040504 1000100 5040504 1000100 5040504 1000100 5040504 2020000 6060404
  //   2020000 6060404 2020000 6060404 2020000 6060404 2020000 6060404 2020000 6060404 2020000 6060404
  //   2020000 6060404 2020000 6060404 2020000 6060404 2020000 6060404 2020000 6060404 2020000 6060404
  //   2020000 6060404 2020000 6060404 2020000 6060404 2020000 6060404 2020000 6060404 2020000 6060404
  //   2020000 6060404 2020000 6060404 2020000 6060404 2020000 6060404 2020000 6060404 2020000 6060404
  //   2020000 6060404 2020000 6060404 2020000 6060404 2020000 6060404 2020000 6060404 2020000 6060404
  //   2020000 6060404 3020100 7060504 3020100 7060504 3020100 7060504 3020100 7060504 3020100 7060504
  //   3020100 7060504 3020100 7060504 3020100 7060504 3020100 7060504 3020100 7060504 3020100 7060504
  //   3020100 7060504 3020100 7060504 3020100 7060504 3020100 7060504 3020100 7060504 3020100 7060504
  //   3020100 7060504 3020100 7060504 3020100 7060504 3020100 7060504 3020100 7060504 3020100 7060504
  //   3020100 7060504 3020100 7060504 3020100 7060504 3020100 7060504 3020100 7060504 3020100 7060504
  //   3020100 7060504 3020100 7060504 3020100 7060504 0 0 8080808 8080808 0 0 8080808 8080808 0 0 8080808
  //   8080808 0 0 8080808 8080808 0 0 8080808 8080808 0 0 8080808 8080808 0 0 8080808 8080808 0 0 8080808
  //   8080808 0 0 8080808 8080808 0 0 8080808 8080808 0 0 8080808 8080808 0 0 8080808 8080808 0 0 8080808
  //   8080808 0 0 8080808 8080808 0 0 8080808 8080808 0 0 8080808 8080808 1000100 1000100 9080908 9080908
  //   1000100 1000100 9080908 9080908 1000100 1000100 9080908 9080908 1000100 1000100 9080908 9080908
  //   1000100 1000100 9080908 9080908 1000100 1000100 9080908 9080908 1000100 1000100 9080908 9080908
  //   1000100 1000100 9080908 9080908 1000100 1000100 9080908 9080908 1000100 1000100 9080908 9080908
  //   1000100 1000100 9080908 9080908 1000100 1000100 9080908 9080908 1000100 1000100 9080908 9080908
  //   1000100 1000100 9080908 9080908 1000100 1000100 9080908 9080908 1000100 1000100 9080908 9080908
  //   2020000 2020000 a0a0808 a0a0808 2020000 2020000 a0a0808 a0a0808 2020000 2020000 a0a0808 a0a0808
  //   2020000 2020000 a0a080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
endmodule

module executor (
  input  [31:0] instruction,
  input  [31:0] rdata1,
  input  [31:0] rdata2,
  input  [31:0] next_addr,
  input  [31:0] mem_rdata,
  output [4:0] raddr1,
  output [4:0] raddr2,
  output [4:0] waddr,
  output wenable,
  output [31:0] wdata,
  output [31:0] jump_addr,
  output jump_enable,
  output [31:0] mem_addr,
  output mem_wenable,
  output mem_renable,
  output mem_byte_access,
  output [31:0] mem_wdata
);

  wire add_jump_enable, add_wenable, addi_jump_enable, addi_wenable, is_add, is_addi, is_jalr, is_lbu,
       is_lui, is_lw, is_sb, is_sw, jalr_jump_enable, jalr_wenable, lbu_mem_byte_access, lbu_mem_renable,
       lbu_wenable, lui_wenable, lw_mem_byte_access, lw_mem_renable, lw_mem_wenable, lw_wenable, or_1_out,
       sb_mem_byte_access, sb_mem_wenable, sw_mem_byte_access, sw_mem_wenable;
  wire [2:0] priority_encoder_1_out, select_signal;
  wire [4:0] add_raddr1, add_raddr2, add_waddr, addi_raddr1, addi_raddr2, addi_waddr, jalr_raddr1,
       jalr_raddr2, jalr_waddr, lbu_raddr1, lbu_waddr, lui_waddr, lw_raddr1, lw_waddr, sb_raddr1, sb_raddr2,
       sw_raddr1, sw_raddr2;
  wire [31:0] add_jump_addr, add_wdata, addi_jump_addr, addi_wdata, jalr_jump_addr, jalr_wdata, lbu_mem_addr,
       lbu_wdata, lui_wdata, lw_mem_addr, lw_wdata, sb_mem_addr, sb_mem_wdata, sw_mem_addr, sw_mem_wdata;

  addi_executor addi_executor_1 (
    .instruction(instruction), .rdata1(rdata1), .raddr1(addi_raddr1), .raddr2(addi_raddr2),
    .waddr(addi_waddr), .wenable(addi_wenable), .wdata(addi_wdata), .jump_addr(addi_jump_addr),
    .jump_enable(addi_jump_enable));
  jalr_excutor jalr_excutor_1 (
    .instruction(instruction), .rdata1(rdata1), .next_addr(next_addr), .raddr1(jalr_raddr1),
    .raddr2(jalr_raddr2), .waddr(jalr_waddr), .wenable(jalr_wenable), .wdata(jalr_wdata),
    .jump_addr(jalr_jump_addr), .jump_enable(jalr_jump_enable));
  add_executor add_executor_1 (
    .instruction(instruction), .rdata1(rdata1), .rdata2(rdata2), .raddr1(add_raddr1), .raddr2(add_raddr2),
    .waddr(add_waddr), .wenable(add_wenable), .wdata(add_wdata), .jump_addr(add_jump_addr),
    .jump_enable(add_jump_enable));
  lui_executor lui_executor_1 (.instruction(instruction), .waddr(lui_waddr), .wdata(lui_wdata), .wenable(lui_wenable));
  lw_executor lw_executor_1 (
    .instruction(instruction), .rdata1(rdata1), .mem_rdata(mem_rdata), .waddr(lw_waddr), .wdata(lw_wdata),
    .wenable(lw_wenable), .raddr1(lw_raddr1), .mem_addr(lw_mem_addr), .mem_wenable(lw_mem_wenable),
    .mem_renable(lw_mem_renable), .mem_byte_enable(lw_mem_byte_access));
  sw_executor sw_executor_1 (
    .instruction(instruction), .rdata1(rdata1), .rdata2(rdata2), .raddr1(sw_raddr1), .raddr2(sw_raddr2),
    .mem_addr(sw_mem_addr), .mem_wdata(sw_mem_wdata), .mem_wenable(sw_mem_wenable),
    .mem_byte_access(sw_mem_byte_access));
  lbu_executor lbu_executor_1 (
    .instruction(instruction), .rdata1(rdata1), .mem_rdata(mem_rdata), .waddr(lbu_waddr),
    .wenable(lbu_wenable), .raddr1(lbu_raddr1), .mem_renable(lbu_mem_renable), .mem_addr(lbu_mem_addr),
    .wdata(lbu_wdata), .mem_byte_access(lbu_mem_byte_access));
  sb_executor sb_executor_1 (
    .instruction(instruction), .rdata2(rdata2), .rdata1(rdata1), .mem_wdata(sb_mem_wdata),
    .raddr1(sb_raddr1), .raddr2(sb_raddr2), .mem_wenable(sb_mem_wenable), .mem_addr(sb_mem_addr),
    .mem_byte_access(sb_mem_byte_access));
  Multiplexer #(.select(3), .width(32)) multiplexer_1 (
    .in0({32{1'b0}}), .in1({32{1'b0}}), .in2({32{1'b0}}), .in3({32{1'b0}}), .in4(lw_mem_addr),
    .in5(sw_mem_addr), .in6(lbu_mem_addr), .in7(sb_mem_addr), .out(mem_addr), .sel(select_signal));
  Priority_Encoder priority_encoder_1 (
    .in0(is_addi), .in1(is_jalr), .in2(is_add), .in3(is_lui), .in4(is_lw), .in5(is_sw), .in6(is_lbu),
    .in7(is_sb), .out(priority_encoder_1_out));  // open: en_in, gs, en_out
  or or_1 (or_1_out, is_lbu, is_addi, is_jalr, is_add, is_lui, is_lw, is_sw, is_sb);
  Multiplexer #(.select(3), .width(5)) multiplexer_2 (
    .in0(addi_raddr2), .in1(jalr_raddr2), .in2(add_raddr2), .in3({5{1'b0}}), .in4({5{1'b0}}),
    .in5(sw_raddr2), .in6({5{1'b0}}), .in7(sb_raddr2), .out(raddr2), .sel(select_signal));
  Multiplexer #(.select(3), .width(5)) multiplexer_3 (
    .in0(addi_waddr), .in1(jalr_waddr), .in2(add_waddr), .in3(lui_waddr), .in4(lw_waddr), .in5({5{1'b0}}),
    .in6(lbu_waddr), .in7({5{1'b0}}), .out(waddr), .sel(select_signal));
  Multiplexer #(.select(3), .width(32)) multiplexer_4 (
    .in0(addi_wdata), .in1(jalr_wdata), .in2(add_wdata), .in3(lui_wdata), .in4(lw_wdata), .in5({32{1'b0}}),
    .in6(lbu_wdata), .in7({32{1'b0}}), .out(wdata), .sel(select_signal));
  Multiplexer #(.select(3), .width(32)) multiplexer_5 (
    .in0(addi_jump_addr), .in1(jalr_jump_addr), .in2(add_jump_addr), .in3({32{1'b0}}), .in4({32{1'b0}}),
    .in5({32{1'b0}}), .in6({32{1'b0}}), .in7({32{1'b0}}), .out(jump_addr), .sel(select_signal));
  Multiplexer #(.select(3)) multiplexer_6 (
    .in0(addi_jump_enable), .in1(jalr_jump_enable), .in2(add_jump_enable), .in3(1'b0), .in4(1'b0),
    .in5(1'b0), .in6(1'b0), .in7(1'b0), .out(jump_enable), .sel(select_signal));
  Multiplexer #(.select(3)) multiplexer_7 (
    .in0(1'b0), .in1(1'b0), .in2(1'b0), .in3(1'b0), .in4(lw_mem_wenable), .in5(sw_mem_wenable), .in6(1'b0),
    .in7(sb_mem_wenable), .out(mem_wenable), .sel(select_signal));
  Multiplexer #(.select(3)) multiplexer_8 (
    .in0(1'b0), .in1(1'b0), .in2(1'b0), .in3(1'b0), .in4(lw_mem_renable), .in5(1'b0), .in6(lbu_mem_renable),
    .in7(1'b0), .out(mem_renable), .sel(select_signal));
  Multiplexer #(.select(3)) multiplexer_9 (
    .in0(1'b0), .in1(1'b0), .in2(1'b0), .in3(1'b0), .in4(lw_mem_byte_access), .in5(sw_mem_byte_access),
    .in6(lbu_mem_byte_access), .in7(sb_mem_byte_access), .out(mem_byte_access), .sel(select_signal));
  Multiplexer #(.select(3), .width(32)) multiplexer_10 (
    .in0({32{1'b0}}), .in1({32{1'b0}}), .in2({32{1'b0}}), .in3({32{1'b0}}), .in4({32{1'b0}}),
    .in5(sw_mem_wdata), .in6({32{1'b0}}), .in7(sb_mem_wdata), .out(mem_wdata), .sel(select_signal));
  Multiplexer #(.width(3)) multiplexer_11 (
    .in0(3'b000), .in1(priority_encoder_1_out), .out(select_signal), .sel(or_1_out));
  Multiplexer #(.select(3)) multiplexer_12 (
    .in0(addi_wenable), .in1(jalr_wenable), .in2(add_wenable), .in3(lui_wenable), .in4(lw_wenable),
    .in5(1'b0), .in6(lbu_wenable), .in7(1'b0), .out(wenable), .sel(select_signal));
  Multiplexer #(.select(3), .width(5)) multiplexer_13 (
    .in0(addi_raddr1), .in1(jalr_raddr1), .in2(add_raddr1), .in3({5{1'b0}}), .in4(lw_raddr1),
    .in5(sw_raddr1), .in6(lbu_raddr1), .in7(sb_raddr1), .out(raddr1), .sel(select_signal));
  instruction_identifier instruction_identifier_1 (
    .instruction(instruction), .is_addi(is_addi), .is_jalr(is_jalr), .is_add(is_add), .is_lui(is_lui),
    .is_lw(is_lw), .is_sw(is_sw), .is_lbu(is_lbu), .is_sb(is_sb));
endmodule

module addi_executor (
  input  [31:0] instruction,
  input  [31:0] rdata1,
  output [4:0] raddr1,
  output [4:0] raddr2,
  output [4:0] waddr,
  output wenable,
  output [31:0] wdata,
  output [31:0] jump_addr,
  output jump_enable
);

  wire [11:0] i_decoder_1_imm;
  wire [31:0] bit_extender_1_out;

  i_decoder i_decoder_1 (
    .instruction(instruction), .rd(waddr), .rs1(raddr1), .imm(i_decoder_1_imm));  // open: opcode, funct3
  assign bit_extender_1_out = {{20{i_decoder_1_imm[11]}}, i_decoder_1_imm};  // Bit_Extender bit_extender_1
  Adder #(.width(32)) adder_1 (.a(bit_extender_1_out), .b(rdata1), .out(wdata));  // open: cin, cout

  assign jump_addr = {32{1'b0}};
  assign jump_enable = 1'b0;
  assign raddr2 = {5{1'b0}};
  assign wenable = 1'b1;
endmodule

module jalr_excutor (
  input  [31:0] instruction,
  input  [31:0] rdata1,
  input  [31:0] next_addr,
  output [4:0] raddr1,
  output [4:0] raddr2,
  output [4:0] waddr,
  output wenable,
  output [31:0] wdata,
  output [31:0] jump_addr,
  output jump_enable
);

  wire [11:0] i_decoder_1_imm;
  wire [31:0] bit_extender_1_out;

  i_decoder i_decoder_1 (
    .instruction(instruction), .rd(waddr), .rs1(raddr1), .imm(i_decoder_1_imm));  // open: opcode, funct3
  assign bit_extender_1_out = {{20{i_decoder_1_imm[11]}}, i_decoder_1_imm};  // Bit_Extender bit_extender_1
  Adder #(.width(32)) adder_1 (.a(bit_extender_1_out), .b(rdata1), .out(jump_addr));  // open: cin, cout

  assign jump_enable = 1'b1;
  assign raddr2 = {5{1'b0}};
  assign wdata = next_addr;
  assign wenable = 1'b1;
endmodule

module r_decoder (
  input  [31:0] instruction,
  output [6:0] opcode,
  output [4:0] rd,
  output [2:0] funct3,
  output [4:0] rs1,
  output [4:0] rs2,
  output [6:0] funct7
);


  assign funct3 = instruction[14:12];
  assign funct7 = instruction[31:25];
  assign opcode = instruction[6:0];
  assign rd = instruction[11:7];
  assign rs1 = instruction[19:15];
  assign rs2 = instruction[24:20];
endmodule

module add_executor (
  input  [31:0] instruction,
  input  [31:0] rdata1,
  input  [31:0] rdata2,
  output [4:0] raddr1,
  output [4:0] raddr2,
  output [4:0] waddr,
  output wenable,
  output [31:0] wdata,
  output [31:0] jump_addr,
  output jump_enable
);

  Adder #(.width(32)) adder_1 (.a(rdata1), .b(rdata2), .out(wdata));  // open: cin, cout
  r_decoder r_decoder_1 (
    .instruction(instruction), .rd(waddr), .rs1(raddr1), .rs2(raddr2));  // open: opcode, funct3, funct7

  assign jump_addr = {32{1'b0}};
  assign jump_enable = 1'b0;
  assign wenable = 1'b1;
endmodule

module u_decoder (
  input  [31:0] instruction,
  output [6:0] opcode,
  output [4:0] rd,
  output [19:0] imm
);


  assign imm = instruction[31:12];
  assign opcode = instruction[6:0];
  assign rd = instruction[11:7];
endmodule

module lui_executor (
  input  [31:0] instruction,
  output [4:0] waddr,
  output [31:0] wdata,
  output wenable
);

  u_decoder u_decoder_1 (.instruction(instruction), .rd(waddr), .imm(wdata[31:12]));  // open: opcode

  assign wdata[11:0] = {12{1'b0}};
  assign wenable = 1'b1;
endmodule

module memory (
  input  mem_wenable,
  input  mem_byte_access,
  input  [31:0] mem_wdata,
  input  [31:0] mem_addr,
  input  clk,
  input  reset,
  output [31:0] mem_rdata
);

  wire comparator_1_eq, comparator_1_gt, comparator_2_lt, is_vga, or_1_out, ram_wenable;
  wire [3:0] byte_enable, multiplexer_2_out;
  wire [7:0] col, row;
  wire [31:0] and_1_out, bit_extender_1_out, multiplexer_3_out, offset, ram_1_dout, shifter_1_out,
       shifter_4_out, vga_addr;
  wire [31:8] pixel, shifter_3_out;

  Multiplexer #(.width(32)) multiplexer_1 (.in0({32{1'b0}}), .in1(mem_addr), .out(vga_addr), .sel(is_vga));
  Multiplexer #(.width(4)) multiplexer_2 (
    .in0(4'b1111), .in1(byte_enable), .out(multiplexer_2_out), .sel(mem_byte_access));
  Shifter #(.width(32)) shifter_1 (.in(mem_wdata), .\dist ({mem_addr[1:0], 3'b000}), .out(shifter_1_out));
  Decoder #(.select(2)) decoder_1 (
    .out0(byte_enable[0]), .out1(byte_enable[1]), .out2(byte_enable[2]), .out3(byte_enable[3]),
    .sel(mem_addr[1:0]));  // open: en
  assign bit_extender_1_out = {{2{1'b0}}, mem_addr[31:2]};  // Bit_Extender bit_extender_1
  Multiplexer #(.width(32)) multiplexer_3 (
    .in0(mem_wdata), .in1(shifter_1_out), .out(multiplexer_3_out), .sel(mem_byte_access));
  RAM #(.addrWidth(24), .asyncread("true"), .byteenables("byteEnables"), .dataWidth(32), .\type ("nonvolatile")) ram_1 (
    .addr(bit_extender_1_out[23:0]), .we(ram_wenable), .oe(1'b1), .clk(clk), .din(multiplexer_3_out),
    .dout(ram_1_dout), .be3(multiplexer_2_out[3]), .be2(multiplexer_2_out[2]), .be1(multiplexer_2_out[1]),
    .be0(multiplexer_2_out[0]));
  // RGB_Video #(.cursor("No Cursor"), .height(256), .scale(1), .width(256)) rgb_video_1: pin names not known; wires that end beside it: reset, clk, is_vga, col, row, mem_wdata[23:0]
  Subtractor #(.width(32)) subtractor_1 (.a(vga_addr), .b(32'h20000000), .out(offset));  // open: bin, bout
  Shifter #(.shift("lr"), .width(32)) shifter_2 (.in(offset), .\dist (5'b00010), .out({pixel, col}));
  Shifter #(.shift("lr"), .width(32)) shifter_3 (.in({pixel, col}), .\dist (5'b01000), .out({shifter_3_out, row}));
  Shifter #(.shift("lr"), .width(32)) shifter_4 (
    .in(ram_1_dout), .\dist ({mem_addr[1:0], 3'b000}), .out(shifter_4_out));
  assign and_1_out = shifter_4_out & 32'hff;  // AND_Gate and_1, 32 bits wide
  Comparator #(.mode("unsigned"), .width(32)) comparator_1 (
    .a(mem_addr), .b(32'h20000000), .gt(comparator_1_gt), .eq(comparator_1_eq));  // open: lt
  Comparator #(.mode("unsigned"), .width(32)) comparator_2 (
    .a(mem_addr), .b(32'h20040000), .lt(comparator_2_lt));  // open: gt, eq
  Multiplexer multiplexer_4 (.in0(mem_wenable), .in1(1'b0), .out(ram_wenable), .sel(is_vga));
  Multiplexer #(.width(32)) multiplexer_5 (.in0(ram_1_dout), .in1(and_1_out), .out(mem_rdata), .sel(mem_byte_access));
  or or_1 (or_1_out, comparator_1_gt, comparator_1_eq);
  and and_2 (is_vga, or_1_out, comparator_2_lt);

  // Other names for the same wires on the sheet: mem_data_shift[4:3] = mem_addr[1:0]; pixel[7:0] = col
endmodule

module lw_executor (
  input  [31:0] instruction,
  input  [31:0] rdata1,
  input  [31:0] mem_rdata,
  output [4:0] waddr,
  output [31:0] wdata,
  output wenable,
  output [4:0] raddr1,
  output [31:0] mem_addr,
  output mem_wenable,
  output mem_renable,
  output mem_byte_enable
);

  wire [11:0] i_decoder_1_imm;
  wire [31:0] bit_extender_1_out;

  i_decoder i_decoder_1 (
    .instruction(instruction), .rd(waddr), .rs1(raddr1), .imm(i_decoder_1_imm));  // open: opcode, funct3
  assign bit_extender_1_out = {{20{i_decoder_1_imm[11]}}, i_decoder_1_imm};  // Bit_Extender bit_extender_1
  Adder #(.width(32)) adder_1 (.a(bit_extender_1_out), .b(rdata1), .out(mem_addr));  // open: cin, cout

  assign mem_byte_enable = 1'b0;
  assign mem_renable = 1'b1;
  assign mem_wenable = 1'b0;
  assign wdata = mem_rdata;
  assign wenable = 1'b1;
endmodule

module s_decoder (
  input  [31:0] instruction,
  output [6:0] opcode,
  output [2:0] funct3,
  output [4:0] rs1,
  output [4:0] rs2,
  output [11:0] imm
);


  assign funct3 = instruction[14:12];
  assign imm = {instruction[31:25], instruction[11:7]};
  assign opcode = instruction[6:0];
  assign rs1 = instruction[19:15];
  assign rs2 = instruction[24:20];
endmodule

module sw_executor (
  input  [31:0] instruction,
  input  [31:0] rdata1,
  input  [31:0] rdata2,
  output [4:0] raddr1,
  output [4:0] raddr2,
  output [31:0] mem_addr,
  output [31:0] mem_wdata,
  output mem_wenable,
  output mem_byte_access
);

  wire [11:0] s_decoder_1_imm;
  wire [31:0] bit_extender_1_out;

  s_decoder s_decoder_1 (
    .instruction(instruction), .rs1(raddr1), .rs2(raddr2), .imm(s_decoder_1_imm));  // open: opcode, funct3
  assign bit_extender_1_out = {{20{s_decoder_1_imm[11]}}, s_decoder_1_imm};  // Bit_Extender bit_extender_1
  Adder #(.width(32)) adder_1 (.a(bit_extender_1_out), .b(rdata1), .out(mem_addr));  // open: cin, cout

  assign mem_byte_access = 1'b0;
  assign mem_wdata = rdata2;
  assign mem_wenable = 1'b1;
endmodule

module lbu_executor (
  input  [31:0] instruction,
  input  [31:0] rdata1,
  input  [31:0] mem_rdata,
  output [4:0] waddr,
  output wenable,
  output [4:0] raddr1,
  output mem_renable,
  output [31:0] mem_addr,
  output [31:0] wdata,
  output mem_byte_access
);

  wire [11:0] i_decoder_1_imm;
  wire [31:0] bit_extender_1_out;

  i_decoder i_decoder_1 (
    .instruction(instruction), .rd(waddr), .rs1(raddr1), .imm(i_decoder_1_imm));  // open: opcode, funct3
  assign bit_extender_1_out = {{20{i_decoder_1_imm[11]}}, i_decoder_1_imm};  // Bit_Extender bit_extender_1
  Adder #(.width(32)) adder_1 (.a(bit_extender_1_out), .b(rdata1), .out(mem_addr));  // open: cin, cout

  assign mem_byte_access = 1'b1;
  assign mem_renable = 1'b1;
  assign wdata = mem_rdata;
  assign wenable = 1'b1;
endmodule

module sb_executor (
  input  [31:0] instruction,
  input  [31:0] rdata2,
  input  [31:0] rdata1,
  output [31:0] mem_wdata,
  output [4:0] raddr1,
  output [4:0] raddr2,
  output mem_wenable,
  output [31:0] mem_addr,
  output mem_byte_access
);

  wire [11:0] s_decoder_1_imm;
  wire [31:0] bit_extender_1_out;

  s_decoder s_decoder_1 (
    .instruction(instruction), .rs1(raddr1), .rs2(raddr2), .imm(s_decoder_1_imm));  // open: opcode, funct3
  assign bit_extender_1_out = {{20{s_decoder_1_imm[11]}}, s_decoder_1_imm};  // Bit_Extender bit_extender_1
  Adder #(.width(32)) adder_1 (.a(bit_extender_1_out), .b(rdata1), .out(mem_addr));  // open: cin, cout

  assign mem_byte_access = 1'b1;
  assign mem_wdata = rdata2;
  assign mem_wenable = 1'b1;
endmodule

module cycle_counter (
  input  clk,
  input  reset
);

  wire [31:0] adder_1_out, register_1_q;

  Register #(.width(32)) register_1 (.D(adder_1_out), .en(1'b1), .clk(clk), .Q(register_1_q), .clr(reset));
  Adder #(.width(32)) adder_1 (.a(register_1_q), .b(32'h1), .out(adder_1_out));  // open: cin, cout
endmodule
