// Logisim project sCPU.circ as structural Verilog: 3 circuits, main circuit sCPU
module sCPU (
  input  Reset
);

  wire and_1_out, and_2_out, clock_1_out, clock_2_out, comparator_1_eq, decoder_1_out0, decoder_1_out1,
       decoder_1_out2, decoder_1_out3, not_1_out, not_2_out, not_3_out;
  wire [1:0] multiplexer_1_out, rom_1_data, rom_1_data_2;
  wire [3:0] adder_1_out, multiplexer_2_out, PC_q;
  wire [7:0] adder_2_out, bit_extender_1_out, multiplexer_3_out, multiplexer_4_out, multiplexer_5_out, R0_q,
       R1_q, R2_q, R3_q;
  wire [7:4] rom_1_data_3;

  not not_1 (not_1_out, rom_1_data_3[6]);
  Multiplexer #(.select(2), .width(2)) multiplexer_1 (
    .in0(rom_1_data_3[5:4]), .in1(2'b00), .in2(rom_1_data_3[5:4]), .in3(2'b00), .out(multiplexer_1_out),
    .sel(rom_1_data_3[7:6]));
  Clock clock_1 (.out(clock_1_out));
  and and_1 (and_1_out, not_2_out, and_2_out);
  Decoder #(.select(2)) decoder_1 (
    .out0(decoder_1_out0), .out1(decoder_1_out1), .out2(decoder_1_out2), .out3(decoder_1_out3),
    .sel(multiplexer_1_out), .en(not_1_out));
  Register R0 (.D(multiplexer_5_out), .en(decoder_1_out0), .clk(clock_2_out), .Q(R0_q), .clr(Reset));
  Clock clock_2 (.out(clock_2_out));
  Multiplexer #(.width(4)) multiplexer_2 (
    .in0(adder_1_out), .in1({rom_1_data_3[5:4], rom_1_data_2}), .out(multiplexer_2_out), .sel(and_1_out));
  Register #(.width(4)) PC (.D(multiplexer_2_out), .en(1'b1), .clk(clock_1_out), .Q(PC_q), .clr(Reset));
  and and_2 (and_2_out, rom_1_data_3[6], rom_1_data_3[7]);
  Register R1 (.D(multiplexer_5_out), .en(decoder_1_out1), .clk(clock_2_out), .Q(R1_q), .clr(Reset));
  Adder #(.width(4)) adder_1 (.a(PC_q), .b(4'b0000), .out(adder_1_out), .cin(1'b1));  // open: cout
  ROM #(.addrWidth(4)) rom_1 (.addr(PC_q), .data({rom_1_data_3, rom_1_data_2, rom_1_data}));
  not not_2 (not_2_out, comparator_1_eq);
  Register R2 (.D(multiplexer_5_out), .en(decoder_1_out2), .clk(clock_2_out), .Q(R2_q), .clr(Reset));
  Register R3 (.D(multiplexer_5_out), .en(decoder_1_out3), .clk(clock_2_out), .Q(R3_q), .clr(Reset));
  Multiplexer #(.select(2), .width(8)) multiplexer_3 (
    .in0(R0_q), .in1(R1_q), .in2(R2_q), .in3(R3_q), .out(multiplexer_3_out), .sel(rom_1_data));
  Multiplexer #(.select(2), .width(8)) multiplexer_4 (
    .in0(R0_q), .in1(R1_q), .in2(R2_q), .in3(R3_q), .out(multiplexer_4_out), .sel(rom_1_data_2));
  Adder adder_2 (.a(multiplexer_3_out), .b(multiplexer_4_out), .out(adder_2_out));  // open: cin, cout
  assign bit_extender_1_out = {{4{1'b0}}, {rom_1_data_2, rom_1_data}};  // Bit_Extender bit_extender_1
  not not_3 (not_3_out, rom_1_data_3[6]);
  Comparator comparator_1 (.a(R0_q), .b(multiplexer_3_out), .eq(comparator_1_eq));  // open: gt, lt
  Multiplexer #(.enable("true"), .width(8)) multiplexer_5 (
    .in0(adder_2_out), .in1(bit_extender_1_out), .out(multiplexer_5_out), .sel(rom_1_data_3[7]),
    .en(not_3_out));

  // Notes on the sheet:
  //   opcode
  //   rd
  //   contents of rom_1 (hex, n*v repeats v):
  //   8a 90 a0 b1 17 29 d1 df
  //   compare result
  //   opcode
  //   raddr2
  //   raddr1
  //   addr
  //   rdata1
  //   imm
  //   rdata2
  //   add
  //   r0
  //   wdata
endmodule

module Decoder_1To2 (
  input  in_1,
  output out_2,
  output out_3
);

  not not_1 (out_2, in_1);

  assign out_3 = in_1;
endmodule

module Single_Port_RAM_2_8 (
  input  [7:0] in_1,
  input  [7:0] D_0,
  input  addr,
  input  EN,
  output [7:0] out_5
);

  wire and_1_out, and_2_out, clock_1_out, decoder_1_out0, decoder_1_out1;
  wire [7:0] and_3_out, and_4_out, demultiplexer_1_out0, demultiplexer_1_out1, register_1_q, register_2_q;

  Clock clock_1 (.out(clock_1_out));
  Demultiplexer #(.width(8)) demultiplexer_1 (
    .out0(demultiplexer_1_out0), .out1(demultiplexer_1_out1), .in({8{1'b1}}), .sel(addr));
  Decoder decoder_1 (.out0(decoder_1_out0), .out1(decoder_1_out1), .sel(addr), .en(1'b1));
  and and_1 (and_1_out, decoder_1_out1, EN);
  and and_2 (and_2_out, decoder_1_out0, EN);
  Register register_1 (.D(D_0), .en(and_2_out), .clk(clock_1_out), .Q(register_1_q), .clr(1'b0));
  Register register_2 (.D(in_1), .en(and_1_out), .clk(clock_1_out), .Q(register_2_q), .clr(1'b0));
  assign and_3_out = demultiplexer_1_out0 & register_1_q;  // AND_Gate and_3, 8 bits wide
  assign and_4_out = demultiplexer_1_out1 & register_2_q;  // AND_Gate and_4, 8 bits wide
  assign out_5 = and_3_out | and_4_out;  // OR_Gate or_1, 8 bits wide
endmodule
